# Fritzing sketch ufo wiring sketch (saved by Fritzing 0.9.2b)

parts:
  Adafruit_HUZZAH_ESP8266_Breakout1 = Adafruit HUZZAH ESP8266 Breakout [part_number=2471]
  S4 = Momentary Switch [package=ksa_sealed_tac_switch]
  CONN1 = USB connector [package=THT]
  J1 = female pin header, 1 pin [form="♀ (female)"]
  J2 = female pin header, 1 pin [form="♀ (female)"]
  J3 = male pin header, 5 pins [form="♂ (male)"]
  LPD8806_RGB_LED_Strip2 = LPD8806 RGB LED Strip
  LPD8806_RGB_LED_Strip3 = LPD8806 RGB LED Strip
  LPD8806_RGB_LED_Strip4 = LPD8806 RGB LED Strip
  LPD8806_RGB_LED_Strip5 = LPD8806 RGB LED Strip

nets:
  GND: Adafruit_HUZZAH_ESP8266_Breakout1.GND, CONN1.GND, CONN1.chassis5, CONN1.chassis6, J2.pin1, J3.pin5, LPD8806_RGB_LED_Strip2.GND, LPD8806_RGB_LED_Strip3.GND, LPD8806_RGB_LED_Strip5.GND#0
  +5V: Adafruit_HUZZAH_ESP8266_Breakout1.VBat, CONN1.d-, J1.pin1, LPD8806_RGB_LED_Strip2.+5V, LPD8806_RGB_LED_Strip3.+5V, LPD8806_RGB_LED_Strip5.+5V#3
  N1: Adafruit_HUZZAH_ESP8266_Breakout1.#14, LPD8806_RGB_LED_Strip2.CI, LPD8806_RGB_LED_Strip3.CI, LPD8806_RGB_LED_Strip5.CI
  N2: Adafruit_HUZZAH_ESP8266_Breakout1.#5, LPD8806_RGB_LED_Strip2.DI
  N3: Adafruit_HUZZAH_ESP8266_Breakout1.#4, LPD8806_RGB_LED_Strip3.DI
  N4: Adafruit_HUZZAH_ESP8266_Breakout1.#2, LPD8806_RGB_LED_Strip5.DI
  N5: Adafruit_HUZZAH_ESP8266_Breakout1.#15, S4.2
  N6: Adafruit_HUZZAH_ESP8266_Breakout1.3V, S4.1
  N7: Adafruit_HUZZAH_ESP8266_Breakout1.V+, J3.pin3
  N8: Adafruit_HUZZAH_ESP8266_Breakout1.RX, J3.pin2
  N9: Adafruit_HUZZAH_ESP8266_Breakout1.TX, J3.pin1
  N10: LPD8806_RGB_LED_Strip4.GND, LPD8806_RGB_LED_Strip5.GND#4
  N11: LPD8806_RGB_LED_Strip4.DI, LPD8806_RGB_LED_Strip5.DO
  N12: LPD8806_RGB_LED_Strip4.CI, LPD8806_RGB_LED_Strip5.CO
  N13: LPD8806_RGB_LED_Strip4.+5V, LPD8806_RGB_LED_Strip5.+5V#7

notes:
  strip 15 leds - upper ring
  strip 15 leds - lower ring
  2 strips 2 leds each - downlight
  wifi reset button
  2000mA 5V power supply
  FTDI connector
  Dynatrace UFO

custom parts:
  LPD8806 RGB LED Strip: Digitally addressable RGB LED strip
